# Fritzing sketch HorusCamV3 (saved by Fritzing 0.8.7b)
circuit board: 8.23972cm x 6.11245cm
breadboards: 1

parts:
  Arduino_Nano = Arduino Nano (Rev3.0)
  100_K = Resistor [tolerance=±5% resistance=220 package=THT]
  0_1_uF = Capacitor [package=cap-pth-small-kit]
  GND_RX_TX = mystery part, 3 pins [chip_label="Extencion TTL"]
  R3_R2_R1 = mystery part, 3 pins [chip_label=?]
  +5_GND = mystery part, 3 pins [chip_label=?]
  VIN = mystery part, 3 pins [chip_label=?]
  IN_GND_+6V = mystery part, 3 pins [chip_label=?]
  SDA_SCL_+5_GND = mystery part, 3 pins [chip_label=?]
  U1 = mystery part, 3 pins [chip_label=?]
  GND_SGN = mystery part, 3 pins [chip_label=?]
  D_+5_GND = mystery part, 3 pins [chip_label=?]
  ESP32-cam = ESP32 - CAM

nets:
  N1: Arduino_Nano.D1/TX, GND_RX_TX.pin1
  N2: Arduino_Nano.D0/RX, GND_RX_TX.pin2
  N3: Arduino_Nano.D2, R3_R2_R1.pin1
  N4: Arduino_Nano.D3, R3_R2_R1.pin2
  N5: Arduino_Nano.D4, R3_R2_R1.pin3
  N6: Arduino_Nano.D5, D_+5_GND.pin3
  N7: Arduino_Nano.D8, GND_SGN.pin1
  N8: Arduino_Nano.D10, ESP32-cam.VOR
  N9: Arduino_Nano.D11/MOSI, ESP32-cam.VOT
  VIN: Arduino_Nano.VIN, VIN.pin2, IN_GND_+6V.pin1, ESP32-cam.5V
  N10: Arduino_Nano.GND, 100_K.Pin_0, +5_GND.pin2, VIN.pin1, IN_GND_+6V.pin2, U1.pin1, GND_SGN.pin3, D_+5_GND.pin1
  N11: Arduino_Nano.5V, U1.pin2
  N12: Arduino_Nano.A5, SDA_SCL_+5_GND.pin2
  N13: Arduino_Nano.A4, SDA_SCL_+5_GND.pin3
  N14: Arduino_Nano.A0, 0_1_uF.2
  N15: 100_K.Pin_1, 0_1_uF.1, IN_GND_+6V.pin3
  N16: GND_RX_TX.pin3, VIN.pin3, ESP32-cam.GND
  N17: +5_GND.pin3, SDA_SCL_+5_GND.pin1, D_+5_GND.pin2

custom parts:
  ESP32 - CAM: The ESP32-CAM has a very competitive small-size camera module that can operate independently as a minimum system with a footprint of only 27*40.5*4.5mm and a deep sleep current of up to 6mA.
